# Fritzing sketch Sparkles (saved by Fritzing 0.9.3b)
breadboards: 1

parts:
  Raspberry_Pi1 = Raspberry Pi Zero
  LED1 = RGB LED (com. cathode, rgb) [package="5 mm [THT]"]
  R1 = Resistor [tolerance=±5% resistance=220 package=THT]
  S1 = Pushbutton [package="[THT]"]

nets:
  N1: Raspberry_Pi1.GIPO17, LED1.red_anode
  N2: Raspberry_Pi1.GIPO27, LED1.green_anode
  N3: Raspberry_Pi1.GIPO22, LED1.blue_anode
  N4: Raspberry_Pi1.GIPO10, S1.Pin_1, S1.Pin_2
  N5: Raspberry_Pi1.GND, R1.Pin_0, S1.Pin_3, S1.Pin_4
  N6: LED1.common_cathode, R1.Pin_1

notes:
  The common cathode of the RGB LED is connected to GND of the PI via a 330 Ohm resistor.

custom parts:
  Raspberry Pi Zero: The Raspberry Pi Zero is the latest single board computer to be released by the Raspberry Pi Foundation. It is the entry level model Raspberry Pi perfect for hobbyists, makers and industrial engineers looking to create solutions where small size and low power consumption are important. This is especially relevant for applications in the wearables space as well as up and coming applications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
